// Logisim project control-logic.circ as structural Verilog: 1 circuit, main circuit control_logic
module control_logic (
  input  [31:0] Instruction,
  input  BrEq,
  input  BrLt,
  output PCSel,
  output RegWEn,
  output [2:0] ImmSel,
  output BrUn,
  output ASel,
  output BSel,
  output [3:0] ALUSel,
  output MemWEn,
  output [1:0] WBSel
);

  wire add, addi, and_24_out, and_34_out, and_35_out, and_36_out, and_37_out, and_38_out, and_inst, andi,
       Auipc, B, beq, bge, bgeu, blt, bltu, bne, f0, f1, f32, five, four, I_loadstore, I_shiftimm, Jal, Jalr,
       lb, lh, Lui, lw, mul, mulh, mulhu, not_1_out, not_2_out, not_3_out, one, or_inst, ori, R, S, sb,
       seven, sh, six, sll_inst, slli, slt, slti, sra_inst, srai, srl_inst, srli, sub, sw, three, two,
       xor_inst, xori, zero;
  wire [5:0] ROMInput;
  wire [15:14] rom_1_data;

  and and_1 (add, R, zero, f0);
  and and_2 (mul, R, zero, f1);
  and and_3 (sub, R, zero, f32);
  and and_4 (sll_inst, R, one, f0);
  and and_5 (mulh, R, one, f1);
  and and_6 (mulhu, R, three, f1);
  and and_7 (slt, R, two, f0);
  and and_8 (xor_inst, R, four, f0);
  and and_9 (srl_inst, R, five, f0);
  and and_10 (sra_inst, R, five, f32);
  and and_11 (or_inst, R, six, f0);
  and and_12 (and_inst, R, seven, f0);
  ROM #(.addrWidth(6), .dataWidth(16)) rom_1 (
    .addr(ROMInput), .data({rom_1_data, WBSel, MemWEn, ALUSel, BSel, ASel, BrUn, ImmSel, RegWEn}));
  Comparator #(.width(3)) comparator_1 (.a(Instruction[14:12]), .b(3'b000), .eq(zero));  // open: gt, lt
  Comparator #(.width(3)) comparator_2 (.a(Instruction[14:12]), .b(3'b001), .eq(one));  // open: gt, lt
  Comparator #(.width(3)) comparator_3 (.a(Instruction[14:12]), .b(3'b010), .eq(two));  // open: gt, lt
  Comparator #(.width(3)) comparator_4 (.a(Instruction[14:12]), .b(3'b011), .eq(three));  // open: gt, lt
  Comparator #(.width(3)) comparator_5 (.a(Instruction[14:12]), .b(3'b100), .eq(four));  // open: gt, lt
  Comparator #(.width(3)) comparator_6 (.a(Instruction[14:12]), .b(3'b101), .eq(five));  // open: gt, lt
  Comparator #(.width(3)) comparator_7 (.a(Instruction[14:12]), .b(3'b110), .eq(six));  // open: gt, lt
  Comparator #(.width(3)) comparator_8 (.a(Instruction[14:12]), .b(3'b111), .eq(seven));  // open: gt, lt
  and and_13 (lb, I_loadstore, zero);
  and and_14 (lh, I_loadstore, one);
  and and_15 (lw, I_loadstore, two);
  and and_16 (addi, I_shiftimm, zero);
  and and_17 (slli, I_shiftimm, one, f0);
  and and_18 (srli, I_shiftimm, five, f0);
  and and_19 (srai, I_shiftimm, five, f32);
  and and_20 (slti, I_shiftimm, two);
  and and_21 (xori, I_shiftimm, four);
  and and_22 (ori, I_shiftimm, six);
  and and_23 (andi, I_shiftimm, seven);
  Comparator #(.width(7)) comparator_9 (.a(Instruction[6:0]), .b(7'b0110011), .eq(R));  // open: gt, lt
  Comparator #(.width(7)) comparator_10 (.a(Instruction[6:0]), .b(7'b0010011), .eq(I_shiftimm));  // open: gt, lt
  Comparator #(.width(7)) comparator_11 (.a(Instruction[6:0]), .b(7'b0000011), .eq(I_loadstore));  // open: gt, lt
  Comparator #(.width(7)) comparator_12 (.a(Instruction[6:0]), .b(7'b0100011), .eq(S));  // open: gt, lt
  Comparator #(.width(7)) comparator_13 (.a(Instruction[6:0]), .b(7'b1100011), .eq(B));  // open: gt, lt
  Comparator #(.width(7)) comparator_14 (.a(Instruction[6:0]), .b(7'b1101111), .eq(Jal));  // open: gt, lt
  Comparator #(.width(7)) comparator_15 (.a(Instruction[6:0]), .b(7'b1100111), .eq(Jalr));  // open: gt, lt
  Comparator #(.width(7)) comparator_16 (.a(Instruction[6:0]), .b(7'b0010111), .eq(Auipc));  // open: gt, lt
  Comparator #(.width(7)) comparator_17 (.a(Instruction[6:0]), .b(7'b0110111), .eq(Lui));  // open: gt, lt
  not not_1 (not_1_out, BrLt);
  and and_24 (and_24_out, bgeu, not_1_out);
  or or_1 (PCSel, and_24_out, and_34_out, and_36_out, and_38_out, and_37_out, and_35_out, Jalr, Jal);
  and and_25 (sb, S, zero);
  and and_26 (sh, S, one);
  and and_27 (sw, S, two);
  and and_28 (beq, B, zero);
  and and_29 (bne, B, one);
  and and_30 (blt, B, four);
  and and_31 (bge, B, five);
  and and_32 (bltu, B, six);
  and and_33 (bgeu, B, seven);
  not not_2 (not_2_out, BrLt);
  and and_34 (and_34_out, bge, not_2_out);
  and and_35 (and_35_out, blt, BrLt);
  Comparator #(.width(7)) comparator_18 (.a(Instruction[31:25]), .b({7{1'b0}}), .eq(f0));  // open: gt, lt
  Comparator #(.width(7)) comparator_19 (.a(Instruction[31:25]), .b(7'b0100000), .eq(f32));  // open: gt, lt
  Comparator #(.width(7)) comparator_20 (.a(Instruction[31:25]), .b(7'b0000001), .eq(f1));  // open: gt, lt
  // Priority_Encoder #(.select_enc(6)) priority_encoder_1: pin names not known; wires that end beside it: ROMInput, add, mul, sub, sll_inst, mulh, mulhu, slt, xor_inst, srl_inst, sra_inst, or_inst, and_inst, lb, lh, lw, addi, slli, slti, xori, srli, srai, ori, andi, sb, sh, sw, beq, bne, blt, bge, bltu, bgeu, Auipc, Lui, Jal, Jalr
  and and_36 (and_36_out, bne, not_3_out);
  and and_37 (and_37_out, bltu, BrLt);
  not not_3 (not_3_out, BrEq);
  and and_38 (and_38_out, beq, BrEq);

  // Other names for the same wires on the sheet: opcode[6:0] = Instruction[6:0]; f3[2:0] = Instruction[14:12];
  //   f7[6:0] = Instruction[31:25]

  // Notes on the sheet:
  //   INPUTS to your circuit
  //   Connect ROM Input here ->
  //   contents of rom_1 (hex, n*v repeats v):
  //   1001 1401 1601 1081 1481 1581 1101 1201 1281 1681 1301 1381 41 41 41 1041 10c1 1141 1241 12c1 16c1
  //   1341 13c1 842 842 842 4*64 74 74 1067 17e7 2069 2041 2041
  //   ROM FOR CONTROL LOGIC
  //   DON'T CHANGE THE LOCATIONS OF THE INPUTS AND OUTPUTS!
  //   This is only if you choose to do the ROM option
  //   CONNECT
  //   WIRE
  //   TO
  //   USE
  //   ROM
  //   OUTPUT from your circuit
  //   Reminder: If using ROM, use combinational logic for PCSel
endmodule
