// Logisim project partial-load.circ as structural Verilog: 1 circuit, main circuit partial_load
module partial_load (
  input  [31:0] Instruction,
  input  [31:0] MemAddress,
  input  [31:0] DataFromMem,
  output [31:0] DataToReg
);

  wire comparator_1_eq, comparator_2_eq, comparator_2_gt, comparator_2_lt, isLb, isLh, isLw;
  wire [1:0] bot_2;
  wire [7:0] multiplexer_1_out;
  wire [15:0] multiplexer_2_out;
  wire [31:0] and_1_out, and_2_out, and_3_out, bit_extender_2_out, bit_extender_3_out, bit_extender_4_out,
       \byte , half;

  Bit_Extender #(.in_width(32), .out_width(2)) bit_extender_1 (.in(MemAddress), .out(bot_2));
  assign bit_extender_2_out = {{31{isLb}}, isLb};  // Bit_Extender bit_extender_2
  assign bit_extender_3_out = {{31{isLh}}, isLh};  // Bit_Extender bit_extender_3
  assign bit_extender_4_out = {{31{isLw}}, isLw};  // Bit_Extender bit_extender_4
  assign and_1_out = \byte  & bit_extender_2_out;  // AND_Gate and_1, 32 bits wide
  assign and_2_out = half & bit_extender_3_out;  // AND_Gate and_2, 32 bits wide
  assign and_3_out = DataFromMem & bit_extender_4_out;  // AND_Gate and_3, 32 bits wide
  Comparator #(.width(7)) comparator_1 (.a(Instruction[6:0]), .b(7'b0000011), .eq(comparator_1_eq));  // open: gt, lt
  Comparator #(.width(3)) comparator_2 (
    .a(Instruction[14:12]), .b(3'b001), .gt(comparator_2_gt), .eq(comparator_2_eq), .lt(comparator_2_lt));
  assign DataToReg = and_1_out | and_2_out | and_3_out;  // OR_Gate or_1, 32 bits wide
  and and_4 (isLw, comparator_1_eq, comparator_2_gt);
  and and_5 (isLh, comparator_1_eq, comparator_2_eq);
  and and_6 (isLb, comparator_1_eq, comparator_2_lt);
  assign \byte  = {{24{multiplexer_1_out[7]}}, multiplexer_1_out};  // Bit_Extender bit_extender_5
  Multiplexer #(.select(2), .width(8)) multiplexer_1 (
    .in0(DataFromMem[7:0]), .in1(DataFromMem[15:8]), .in2(DataFromMem[23:16]), .in3(DataFromMem[31:24]),
    .out(multiplexer_1_out), .sel(bot_2));
  Multiplexer #(.select(2), .width(16)) multiplexer_2 (
    .in0(DataFromMem[15:0]), .in1(DataFromMem[23:8]), .in2(DataFromMem[31:16]), .out(multiplexer_2_out),
    .sel(bot_2));  // open: in3
  assign half = {{16{multiplexer_2_out[15]}}, multiplexer_2_out};  // Bit_Extender bit_extender_6

  // Other names for the same wires on the sheet: word[31:0] = DataFromMem; opcode[6:0] = Instruction[6:0];
  //   funct3[2:0] = Instruction[14:12]

  // Notes on the sheet:
  //   INPUTS to your circuit
  //   DON'T CHANGE THE LOCATIONS OF THE INPUTS AND OUTPUTS!
  //   OUTPUT from your circuit
endmodule
