// Logisim project partial-store.circ as structural Verilog: 1 circuit, main circuit partial_store
module partial_store (
  input  [31:0] Instruction,
  input  [31:0] MemAddress,
  input  [31:0] DataFromReg,
  input  MemWEn,
  output [3:0] MemWriteMask,
  output [31:0] DataToMem
);

  wire comparator_1_eq, comparator_2_eq, comparator_2_gt, comparator_2_lt, isSb, isSh, isSw;
  wire [1:0] bot_2;
  wire [3:0] and_7_out, and_8_out, and_9_out, bit_extender_7_out, bit_extender_8_out, bit_extender_9_out,
       bit_extender_10_out, bit_extender_11_out, bit_extender_12_out, byteMasks, half_wordMasks, or_2_out;
  wire [7:0] bit_extender_6_out;
  wire [15:0] bit_extender_5_out;
  wire [31:0] and_1_out, and_2_out, and_3_out, bit_extender_2_out, bit_extender_3_out, bit_extender_4_out,
       \byte , half_word;

  Bit_Extender #(.in_width(32), .out_width(2)) bit_extender_1 (.in(MemAddress), .out(bot_2));
  assign bit_extender_2_out = {{31{isSw}}, isSw};  // Bit_Extender bit_extender_2
  assign bit_extender_3_out = {{31{isSh}}, isSh};  // Bit_Extender bit_extender_3
  assign bit_extender_4_out = {{31{isSb}}, isSb};  // Bit_Extender bit_extender_4
  assign and_1_out = bit_extender_2_out & DataFromReg;  // AND_Gate and_1, 32 bits wide
  assign and_2_out = bit_extender_3_out & half_word;  // AND_Gate and_2, 32 bits wide
  assign and_3_out = bit_extender_4_out & \byte ;  // AND_Gate and_3, 32 bits wide
  Comparator #(.width(7)) comparator_1 (.a(Instruction[6:0]), .b(7'b0100011), .eq(comparator_1_eq));  // open: gt, lt
  Comparator #(.width(3)) comparator_2 (
    .a(Instruction[14:12]), .b(3'b001), .gt(comparator_2_gt), .eq(comparator_2_eq), .lt(comparator_2_lt));
  assign DataToMem = and_1_out | and_2_out | and_3_out;  // OR_Gate or_1, 32 bits wide
  and and_4 (isSw, comparator_1_eq, comparator_2_gt);
  and and_5 (isSh, comparator_1_eq, comparator_2_eq);
  and and_6 (isSb, comparator_1_eq, comparator_2_lt);
  Bit_Extender #(.in_width(32)) bit_extender_5 (.in(DataFromReg), .out(bit_extender_5_out));
  Bit_Extender #(.in_width(32), .out_width(8)) bit_extender_6 (.in(DataFromReg), .out(bit_extender_6_out));
  Multiplexer #(.select(2), .width(32)) multiplexer_1 (
    .in0({{16{1'b0}}, bit_extender_5_out}), .in2({bit_extender_5_out, {16{1'b0}}}), .out(half_word),
    .sel(bot_2));  // open: in1, in3
  Multiplexer #(.select(2), .width(32)) multiplexer_2 (
    .in0({{24{1'b0}}, bit_extender_6_out}), .in1({{16{1'b0}}, bit_extender_6_out, {8{1'b0}}}),
    .in2({{8{1'b0}}, bit_extender_6_out, {16{1'b0}}}), .in3({bit_extender_6_out, {24{1'b0}}}), .out(\byte ),
    .sel(bot_2));
  Multiplexer #(.select(2), .width(4)) multiplexer_3 (
    .in0(4'b0001), .in1(4'b0010), .in2(4'b0100), .in3(4'b1000), .out(byteMasks), .sel(bot_2));
  Multiplexer #(.select(2), .width(4)) multiplexer_4 (
    .in0(4'b0011), .in2(4'b1100), .out(half_wordMasks), .sel(bot_2));  // open: in1, in3
  assign bit_extender_7_out = {{3{isSw}}, isSw};  // Bit_Extender bit_extender_7
  assign bit_extender_8_out = {{3{MemWEn}}, MemWEn};  // Bit_Extender bit_extender_8
  assign bit_extender_9_out = {{3{isSh}}, isSh};  // Bit_Extender bit_extender_9
  assign bit_extender_10_out = {{3{MemWEn}}, MemWEn};  // Bit_Extender bit_extender_10
  assign bit_extender_11_out = {{3{isSb}}, isSb};  // Bit_Extender bit_extender_11
  assign bit_extender_12_out = {{3{MemWEn}}, MemWEn};  // Bit_Extender bit_extender_12
  assign and_7_out = bit_extender_7_out & bit_extender_8_out & 4'b1111;  // AND_Gate and_7, 4 bits wide
  assign and_8_out = bit_extender_9_out & bit_extender_10_out & half_wordMasks;  // AND_Gate and_8, 4 bits wide
  assign and_9_out = bit_extender_11_out & bit_extender_12_out & byteMasks;  // AND_Gate and_9, 4 bits wide
  assign or_2_out = and_7_out | and_8_out | and_9_out;  // OR_Gate or_2, 4 bits wide
  Multiplexer #(.width(4)) multiplexer_5 (.in0(4'b0000), .in1(or_2_out), .out(MemWriteMask), .sel(MemWEn));

  // Other names for the same wires on the sheet: opcode[6:0] = Instruction[6:0]; funct3[2:0] = Instruction[14:12];
  //   word[31:0] = DataFromReg

  // Notes on the sheet:
  //   INPUTS to your circuit
  //   DON'T CHANGE THE LOCATIONS OF THE INPUTS AND OUTPUTS!
  //   OUTPUT from your circuit
endmodule
